// Logisim project Behrmann_Quinn.circ as structural Verilog: 7 circuits, main circuit MAXV_CHENILLARD
module MAXV_CHENILLARD (
  input  load_i,
  input  [7:0] switch_i,
  input  clk_i,
  input  nReset_i,
  output [7:0] led_o
);

  wire entree_i_sw7, entree_i_sw8, not_1_out;
  wire [1:0] entree_i_sw2;

  DipSwitch entree_i (
    .sw1(entree_i_sw2[1]), .sw2(entree_i_sw2[0]), .sw7(entree_i_sw7), .sw8(entree_i_sw8));  // open: sw3, sw4, sw5, sw6
  not not_1 (not_1_out, nReset_i);
  chenillard_TOP chenillard_top_1 (
    .load_i(load_i), .enable_i(entree_i_sw7), .right_nleft_i(entree_i_sw8), .speed_i(entree_i_sw2),
    .val_i(switch_i), .clk_i(clk_i), .reset_i(not_1_out), .led_o(led_o));

  // Notes on the sheet:
  //   Attention, votre version de Logisim
  //   ne contient pas de tracker. Si vous
  //   enregistrez votre projet, toutes les
  //   informations du tracker seront
  //   définitivement effacées.
endmodule

module chenillard_TOP (
  input  load_i,
  input  enable_i,
  input  right_nleft_i,
  input  [1:0] speed_i,
  input  [7:0] val_i,
  input  clk_i,
  input  reset_i,
  output [7:0] led_o
);

  wire and_2_out, not_1_out, or_2_out, timer_28b_1_done_o;
  wire [1:0] or_1_out;
  wire [27:0] multiplexer_1_out;

  Multiplexer #(.select(2), .width(28), .enable("false")) multiplexer_1 (
    .in0(28'h7270e0), .in1(28'he4e1c0), .in2(28'h1c9c380), .in3(28'h3938700), .out(multiplexer_1_out),
    .sel(speed_i));
  and and_1 (or_1_out[1], timer_28b_1_done_o, not_1_out, enable_i);
  not not_1 (not_1_out, load_i);
  and and_2 (and_2_out, timer_28b_1_done_o, enable_i, right_nleft_i);
  or or_1 (or_1_out[0], and_2_out, load_i);
  or or_2 (or_2_out, load_i, enable_i);
  timer_28b timer_28b_1 (
    .load_i(timer_28b_1_done_o), .value_i(multiplexer_1_out), .en_i(or_2_out), .clk_i(clk_i),
    .reset_i(reset_i), .done_o(timer_28b_1_done_o));
  shift_reg_8b shift_reg_8b_1 (
    .ser_r_i(led_o[0]), .ser_l_i(led_o[7]), .value_load_i(val_i), .mode_i(or_1_out), .clk_i(clk_i),
    .reset_i(reset_i), .val_o(led_o));

  // Notes on the sheet:
  //   Attention, votre version de Logisim
  //   ne contient pas de tracker. Si vous
  //   enregistrez votre projet, toutes les
  //   informations du tracker seront
  //   définitivement effacées.
endmodule

module shift_reg_4b (
  input  ser_l_i,
  input  ser_r_i,
  input  [1:0] mode_i,
  input  [3:0] value_load_i,
  input  clk_i,
  input  reset_i,
  output [3:0] val_o
);

  wire multiplexer_1_out, multiplexer_2_out, multiplexer_3_out, multiplexer_4_out;

  Multiplexer #(.select(2), .enable("false")) multiplexer_1 (
    .in0(val_o[3]), .in1(value_load_i[3]), .in2(val_o[2]), .in3(ser_r_i), .out(multiplexer_1_out),
    .sel(mode_i));
  D_Flip_Flop d_ff_1 (.D(multiplexer_1_out), .clk(clk_i), .Q(val_o[3]), .reset(reset_i));  // open: Qn, preset
  Multiplexer #(.select(2), .enable("false")) multiplexer_2 (
    .in0(val_o[2]), .in1(value_load_i[2]), .in2(val_o[1]), .in3(val_o[3]), .out(multiplexer_2_out),
    .sel(mode_i));
  D_Flip_Flop d_ff_2 (.D(multiplexer_2_out), .clk(clk_i), .Q(val_o[2]), .reset(reset_i));  // open: Qn, preset
  Multiplexer #(.select(2), .enable("false")) multiplexer_3 (
    .in0(val_o[1]), .in1(value_load_i[1]), .in2(val_o[0]), .in3(val_o[2]), .out(multiplexer_3_out),
    .sel(mode_i));
  D_Flip_Flop d_ff_3 (.D(multiplexer_3_out), .clk(clk_i), .Q(val_o[1]), .reset(reset_i));  // open: Qn, preset
  Multiplexer #(.select(2), .enable("false")) multiplexer_4 (
    .in0(val_o[0]), .in1(value_load_i[0]), .in2(ser_l_i), .in3(val_o[1]), .out(multiplexer_4_out),
    .sel(mode_i));
  D_Flip_Flop d_ff_4 (.D(multiplexer_4_out), .clk(clk_i), .Q(val_o[0]), .reset(reset_i));  // open: Qn, preset

  // Notes on the sheet:
  //   Attention, votre version de Logisim
  //   ne contient pas de tracker. Si vous
  //   enregistrez votre projet, toutes les
  //   informations du tracker seront
  //   définitivement effacées.
endmodule

module shift_reg_8b (
  input  ser_r_i,
  input  ser_l_i,
  input  [7:0] value_load_i,
  input  [1:0] mode_i,
  input  clk_i,
  input  reset_i,
  output [7:0] val_o
);

  shift_reg_4b shift_reg_4b_1 (
    .ser_l_i(ser_l_i), .ser_r_i(val_o[4]), .mode_i(mode_i), .value_load_i(value_load_i[3:0]), .clk_i(clk_i),
    .reset_i(reset_i), .val_o(val_o[3:0]));
  shift_reg_4b shift_reg_4b_2 (
    .ser_l_i(val_o[3]), .ser_r_i(ser_r_i), .mode_i(mode_i), .value_load_i(value_load_i[7:4]), .clk_i(clk_i),
    .reset_i(reset_i), .val_o(val_o[7:4]));

  // Notes on the sheet:
  //   Attention, votre version de Logisim
  //   ne contient pas de tracker. Si vous
  //   enregistrez votre projet, toutes les
  //   informations du tracker seront
  //   définitivement effacées.
endmodule

module timer_28b (
  input  load_i,
  input  [27:0] value_i,
  input  en_i,
  input  clk_i,
  input  reset_i,
  output done_o
);

  wire [27:0] multiplexer_1_out, reg_28b_1_val_o, subtractor_1_out;

  Subtractor #(.width(28)) subtractor_1 (
    .a(reg_28b_1_val_o), .b(28'h1), .out(subtractor_1_out), .bin(1'b0));  // open: bout
  Multiplexer #(.width(28), .enable("false")) multiplexer_1 (
    .in0(subtractor_1_out), .in1(value_i), .out(multiplexer_1_out), .sel(load_i));
  reg_28b reg_28b_1 (
    .value_load_i(multiplexer_1_out), .en_i(en_i), .clk_i(clk_i), .reset_i(reset_i), .val_o(reg_28b_1_val_o));
  Comparator #(.width(28)) comparator_1 (.a(reg_28b_1_val_o), .b(28'h1), .eq(done_o));  // open: gt, lt

  // Notes on the sheet:
  //   Attention, votre version de Logisim
  //   ne contient pas de tracker. Si vous
  //   enregistrez votre projet, toutes les
  //   informations du tracker seront
  //   définitivement effacées.
endmodule

module chronogram (
  input  r,
  input  l,
  input  [7:0] load,
  input  [1:0] mode,
  input  reset,
  output [7:0] resultat
);

  wire clk_out;

  Clock clk (.out(clk_out));
  Clock sysclk ();  // open: out
  shift_reg_4b shift_reg_4b_1 (
    .ser_l_i(l), .ser_r_i(resultat[4]), .mode_i(mode), .value_load_i(load[3:0]), .clk_i(clk_out),
    .reset_i(reset), .val_o(resultat[3:0]));
  shift_reg_4b shift_reg_4b_2 (
    .ser_l_i(resultat[3]), .ser_r_i(r), .mode_i(mode), .value_load_i(load[7:4]), .clk_i(clk_out),
    .reset_i(reset), .val_o(resultat[7:4]));

  // Notes on the sheet:
  //   Attention, votre version de Logisim
  //   ne contient pas de tracker. Si vous
  //   enregistrez votre projet, toutes les
  //   informations du tracker seront
  //   définitivement effacées.
endmodule

module reg_28b (
  input  [27:0] value_load_i,
  input  en_i,
  input  clk_i,
  input  reset_i,
  output [27:0] val_o
);

  shift_reg_8b shift_reg_8b_1 (
    .ser_r_i(1'b0), .ser_l_i(1'b0), .value_load_i(value_load_i[7:0]), .mode_i({1'b0, en_i}), .clk_i(clk_i),
    .reset_i(reset_i), .val_o(val_o[7:0]));
  shift_reg_8b shift_reg_8b_2 (
    .ser_r_i(1'b0), .ser_l_i(1'b0), .value_load_i(value_load_i[15:8]), .mode_i({1'b0, en_i}), .clk_i(clk_i),
    .reset_i(reset_i), .val_o(val_o[15:8]));
  shift_reg_8b shift_reg_8b_3 (
    .ser_r_i(1'b0), .ser_l_i(1'b0), .value_load_i(value_load_i[23:16]), .mode_i({1'b0, en_i}), .clk_i(clk_i),
    .reset_i(reset_i), .val_o(val_o[23:16]));
  shift_reg_4b shift_reg_4b_1 (
    .ser_l_i(1'b0), .ser_r_i(1'b0), .mode_i({1'b0, en_i}), .value_load_i(value_load_i[27:24]), .clk_i(clk_i),
    .reset_i(reset_i), .val_o(val_o[27:24]));

  // Notes on the sheet:
  //   Attention, votre version de Logisim
  //   ne contient pas de tracker. Si vous
  //   enregistrez votre projet, toutes les
  //   informations du tracker seront
  //   définitivement effacées.
endmodule
